# Fritzing sketch gsclock_arduino_uno_sketch (saved by Fritzing 0.9.6b)
breadboards: 1

parts:
  パーツ1 = Arduino Uno (Rev3) - ICSP
  Part1 = KY-015 Temperature & Humidity Sensor Module [package="Breakout board"]
  LED1 = LED - 5mm [color="Red (633nm)" current=0.030 package="5 mm [THT]"]
  S1 = Pushbutton [package="[THT]"]
  R1 = Resistor [tolerance=±5% power=0.25 resistance=1k package=THT]
  R3 = Photocell (LDR) [package=THT]
  R4 = Resistor [tolerance=±5% power=0.25 resistance=1k package=THT]
  Pulldown_Regsiter = Resistor [tolerance=±5% power=0.25 resistance=10k package=THT]
  SG1 = Buzzer 12mm [part_number=COM-07950 package=buzzer-12mm-ns]
  R5 = Trimmer Potentiometer [maximum_resistance=10kΩ package=THT]

nets:
  N1: パーツ1.A0, R3.pin_1, R4.Pin_0
  N2: パーツ1.D8, R5.leg1
  N3: パーツ1.GND, Part1.-, LED1.cathode, R4.Pin_1, Pulldown_Regsiter.Pin_1, SG1.2, R5.leg2
  N4: パーツ1.D2, S1.Pin_1, S1.Pin_2, Pulldown_Regsiter.Pin_0
  N5: パーツ1.D4, Part1.Vin, R1.Pin_1, R3.pin_0
  N6: パーツ1.D7, Part1.S
  N7: パーツ1.5V, S1.Pin_3, S1.Pin_4
  N8: LED1.anode, R1.Pin_0
  N9: SG1.1, R5.wiper

custom parts:
  KY-015 Temperature & Humidity Sensor Module: DH-11 temperature and humidity sensor in KEYES KY-015 module, provides a low-latency serial interface to measure humidity and temperature.
  Buzzer 12mm: Buzzer 12mm Spark Fun Electronics SKU : Comp-Buzzer Through hole This is a small 12mm round speaker that operates around the audible 2kHz range. You can use these speakers to create simple music or user interfaces. This is not a true piezoelectric speaker but behaves similarly. Instead of a piezoelectric crystal that vibrates with an electric current, this tiny speaker uses an electromagnet to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
